# Fritzing sketch LED (saved by Fritzing 0.9.3b)
breadboards: 1

parts:
  パーツ1 = Arduino Uno (Rev3)
  U1 = LM 358 Dual Op-Amp [package="DIP8 [THT]"]
  R1 = Resistor [tolerance=±5% resistance=1k package=THT]
  R2 = Resistor [tolerance=±5% resistance=330 package=THT]
  R3 = Resistor [tolerance=±5% resistance=330 package="2512 [SMD]"]
  R4 = Resistor [tolerance=±5% resistance=35 package="2512 [SMD]"]
  LED1 = LED - 5mm [color="Red (633nm)" package="5 mm [THT]"]

nets:
  N1: パーツ1.5V, U1.connector7, R1.Pin_1
  N2: パーツ1.GND, U1.connector3, R3.Pin_1, R4.Pin_1
  N3: U1.connector0, LED1.anode
  N4: U1.connector1, R4.Pin_0, LED1.cathode
  N5: U1.connector2, R2.Pin_0, R3.Pin_0
  N6: R1.Pin_0, R2.Pin_1
